# Fritzing sketch TidePoolProposed (saved by Fritzing 0.9.3b)

parts:
  Part2 = Arduino Uno (Rev3) - ICSP
  LED1 = RGB LED (com. cathode, rgb) [package="5 mm [THT]"]
  U3 = RELAY [package=relay-t9a-2]
  U4 = RELAY [package=relay-t9a-2]
  U5 = SPM0204UD5 [package=spm0204ud5]
  J1 = Infrared Proximity Sensor
  Part3 = DeuLigne 1.1 - The Snootlab's LCD shield for Arduino  # not connected

nets:
  5V: Part2.5V, U5.VS, J1.Vcc
  GND: Part2.GND, LED1.common_cathode, U3.COIL2, U4.COIL2, U5.GND, J1.GND
  N1: Part2.D10_PWM/SS, LED1.green_anode
  N2: Part2.D11_PWM/MOSI, LED1.blue_anode
  N3: Part2.D12/MISO, U3.COIL1
  N4: Part2.D13/SCK, U4.COIL1
  N5: Part2.D2, U5.GND#
  N6: Part2.D3_PWM, U5.OUT
  N7: Part2.D4, J1.Vout
  pump2: U3.MAIN
  GND_2: U3.NC, U4.NC
  120V: U3.NO, U4.NO
  pump1: U4.MAIN

notes:
  pump1
  pump2
  ultrasonic sensor
  IR limit sensor
